# Fritzing sketch cc1101example (saved by Fritzing 1.0.1rc)
breadboards: 1

parts:
  U1 = atmega328 [package=dip]
  S1 = Pushbutton [package="[SMD]"]
  HT1 = HT7333 Regulator [package=to-92-ammo]
  C1 = Ceramic Capacitor [capacitance=1µF voltage=35V package="100 mil [THT, multilayer]"]
  C3 = Ceramic Capacitor [capacitance=1µF voltage=35V package="100 mil [THT, multilayer]"]
  C4 = Ceramic Capacitor [capacitance=1µF voltage=35V package="100 mil [THT, multilayer]"]
  C5 = Ceramic Capacitor [capacitance=1µF voltage=35V package="100 mil [THT, multilayer]"]
  LED1 = LED - 3mm [color="Green (565nm)" current=0.030A package="3 mm [THT]"]
  R1 = Resistor [tolerance=±5% resistance=2.2k power=0.25W package=THT]
  D-SUN_CC1101_PINS_AT_BOTTOM = mystery part, 8 pins [chip_label=?]
  S2 = Pushbutton [package="[SMD]"]
  U2 = LIPO-110mAh [package=lipo-110]

nets:
  N1: U1.RESET, S1.Pin_1, S1.Pin_2
  3.3V: U1.VCC, U1.AVCC, HT1.VOUT, C3.1, C4.0, C5.1, D-SUN_CC1101_PINS_AT_BOTTOM.pin4
  GND: U1.GND, S1.Pin_3, S1.Pin_4, HT1.GND, C1.0, C3.0, C4.1, C5.0, LED1.cathode, D-SUN_CC1101_PINS_AT_BOTTOM.pin5, S2.Pin_1, S2.Pin_2, U2.-
  N2: U1.D8, S2.Pin_3, S2.Pin_4
  N3: U1.D9_(PWM), D-SUN_CC1101_PINS_AT_BOTTOM.pin8
  N4: U1.D10_(PWM), D-SUN_CC1101_PINS_AT_BOTTOM.pin1
  N5: U1.D11_(PWM), D-SUN_CC1101_PINS_AT_BOTTOM.pin6
  N6: U1.D12, D-SUN_CC1101_PINS_AT_BOTTOM.pin7
  N7: U1.D13, D-SUN_CC1101_PINS_AT_BOTTOM.pin3
  N8: U1.A3, R1.Pin_1
  4.2V: HT1.VIN, C1.1, U2.+
  N9: LED1.anode, R1.Pin_0

notes:
  Serial Programmer

custom parts:
  HT7333 Regulator: Voltaghe regulator 4uA qiescent current
